// Logisim project Lab_1.circ as structural Verilog: 7 circuits, main circuit main
module main (
  input  in_1,
  input  in_2,
  input  in_3,
  input  in_4,
  input  in_5,
  input  in_6,
  input  in_7,
  input  in_8,
  input  in_9,
  input  in_10,
  input  in_11,
  input  in_12,
  input  in_13,
  input  in_14,
  input  in_15,
  input  in_16,
  input  select,
  input  in_18,
  output out_19,
  output out_20,
  output \output ,
  output out_22,
  output out_23,
  output out_24,
  output out_25,
  output out_26
);

  wire AND_o0, AND_o1, AND_o2, AND_o3, AND_o4, AND_o5, AND_o6, AND_o7, NOT_o0, NOT_o1, NOT_o2, NOT_o3,
       NOT_o4, NOT_o5, NOT_o6, NOT_o7, OR_o0, OR_o1, OR_o2, OR_o3, OR_o4, OR_o5, OR_o6, OR_o7, XOR_o0,
       XOR_o1, XOR_o2, XOR_o3, XOR_o4, XOR_o5, XOR_o6, XOR_o7;

  AND AND (
    .in_9(in_1), .in_10(in_2), .in_11(in_3), .in_12(in_4), .in_13(in_5), .in_14(in_6), .in_15(in_7),
    .in_16(in_8), .in_1(in_9), .in_2(in_10), .in_3(in_11), .in_4(in_12), .in_5(in_13), .in_6(in_14),
    .in_7(in_15), .in_8(in_16), .O0(AND_o0), .O1(AND_o1), .O2(AND_o2), .O3(AND_o3), .O4(AND_o4), .O5(AND_o5),
    .O6(AND_o6), .O7(AND_o7));
  OR OR (
    .in_9(in_9), .in_10(in_10), .in_11(in_11), .in_12(in_12), .in_13(in_13), .in_14(in_14), .in_15(in_15),
    .in_16(in_16), .in_1(in_1), .in_2(in_2), .in_3(in_3), .in_4(in_4), .in_5(in_5), .in_6(in_6), .in_7(in_7),
    .in_8(in_8), .O0(OR_o0), .O1(OR_o1), .O2(OR_o2), .O3(OR_o3), .O4(OR_o4), .O5(OR_o5), .O6(OR_o6),
    .O7(OR_o7));
  XOR XOR (
    .in_9(in_1), .in_10(in_2), .in_11(in_3), .in_12(in_4), .in_13(in_5), .in_14(in_6), .in_15(in_7),
    .in_16(in_8), .in_1(in_9), .in_2(in_10), .in_3(in_11), .in_4(in_12), .in_5(in_13), .in_6(in_14),
    .in_7(in_15), .in_8(in_16), .O0(XOR_o0), .O1(XOR_o1), .O2(XOR_o2), .O3(XOR_o3), .O4(XOR_o4), .O5(XOR_o5),
    .O6(XOR_o6), .O7(XOR_o7));
  NOT NOT (
    .O0(NOT_o0), .O1(NOT_o1), .O2(NOT_o2), .O3(NOT_o3), .O4(NOT_o4), .O5(NOT_o5), .O6(NOT_o6), .O7(NOT_o7),
    .in_5(in_1), .in_6(in_2), .in_7(in_3), .in_8(in_4), .I0(in_5), .in_2(in_6), .in_3(in_7), .in_4(in_8));
  _4_1_MUX u_4_1_mux_1 (
    .in_00(AND_o0), .in_01(OR_o0), .in_10(XOR_o0), .in_11(NOT_o4), .sel_0(select), .sel_1(in_18), .out(out_19));
  _4_1_MUX u_4_1_mux_2 (
    .in_00(AND_o1), .in_01(OR_o1), .in_10(XOR_o1), .in_11(NOT_o5), .sel_0(select), .sel_1(in_18), .out(out_20));
  _4_1_MUX u_4_1_mux_3 (
    .in_00(AND_o2), .in_01(OR_o2), .in_10(XOR_o2), .in_11(NOT_o6), .sel_0(select), .sel_1(in_18),
    .out(\output ));
  _4_1_MUX u_4_1_mux_4 (
    .in_00(AND_o3), .in_01(OR_o3), .in_10(XOR_o3), .in_11(NOT_o7), .sel_0(select), .sel_1(in_18), .out(out_22));
  _4_1_MUX u_4_1_mux_5 (
    .in_00(AND_o4), .in_01(OR_o4), .in_10(XOR_o4), .in_11(NOT_o0), .sel_0(select), .sel_1(in_18), .out(out_23));
  _4_1_MUX u_4_1_mux_6 (
    .in_00(AND_o5), .in_01(OR_o5), .in_10(XOR_o5), .in_11(NOT_o1), .sel_0(select), .sel_1(in_18), .out(out_24));
  _4_1_MUX u_4_1_mux_7 (
    .in_00(AND_o6), .in_01(OR_o6), .in_10(XOR_o6), .in_11(NOT_o2), .sel_0(select), .sel_1(in_18), .out(out_25));
  _4_1_MUX u_4_1_mux_8 (
    .in_00(AND_o7), .in_01(OR_o7), .in_10(XOR_o7), .in_11(NOT_o3), .sel_0(select), .sel_1(in_18), .out(out_26));

  // Notes on the sheet:
  //   input
endmodule

module AND (
  input  in_1,
  input  in_2,
  input  in_3,
  input  in_4,
  input  in_5,
  input  in_6,
  input  in_7,
  input  in_8,
  input  in_9,
  input  in_10,
  input  in_11,
  input  in_12,
  input  in_13,
  input  in_14,
  input  in_15,
  input  in_16,
  output O0,
  output O1,
  output O2,
  output O3,
  output O4,
  output O5,
  output O6,
  output O7
);

  and and_1 (O0, in_1, in_9);
  and and_2 (O1, in_2, in_10);
  and and_3 (O2, in_3, in_11);
  and and_4 (O3, in_4, in_12);
  and and_5 (O4, in_5, in_13);
  and and_6 (O5, in_6, in_14);
  and and_7 (O6, in_7, in_15);
  and and_8 (O7, in_8, in_16);

  // Notes on the sheet:
  //   I0
  //   I1
endmodule

module OR (
  input  in_1,
  input  in_2,
  input  in_3,
  input  in_4,
  input  in_5,
  input  in_6,
  input  in_7,
  input  in_8,
  input  in_9,
  input  in_10,
  input  in_11,
  input  in_12,
  input  in_13,
  input  in_14,
  input  in_15,
  input  in_16,
  output O0,
  output O1,
  output O2,
  output O3,
  output O4,
  output O5,
  output O6,
  output O7
);

  or or_1 (O0, in_1, in_9);
  or or_2 (O1, in_2, in_10);
  or or_3 (O2, in_3, in_11);
  or or_4 (O3, in_4, in_12);
  or or_5 (O4, in_5, in_13);
  or or_6 (O5, in_6, in_14);
  or or_7 (O6, in_7, in_15);
  or or_8 (O7, in_8, in_16);

  // Notes on the sheet:
  //   I0
  //   I1
endmodule

module NOT (
  input  I0,
  input  in_2,
  input  in_3,
  input  in_4,
  input  in_5,
  input  in_6,
  input  in_7,
  input  in_8,
  output O0,
  output O1,
  output O2,
  output O3,
  output O4,
  output O5,
  output O6,
  output O7
);

  not not_1 (O0, I0);
  not not_2 (O1, in_2);
  not not_3 (O2, in_3);
  not not_4 (O3, in_4);
  not not_5 (O4, in_5);
  not not_6 (O5, in_6);
  not not_7 (O6, in_7);
  not not_8 (O7, in_8);
endmodule

module XOR (
  input  in_1,
  input  in_2,
  input  in_3,
  input  in_4,
  input  in_5,
  input  in_6,
  input  in_7,
  input  in_8,
  input  in_9,
  input  in_10,
  input  in_11,
  input  in_12,
  input  in_13,
  input  in_14,
  input  in_15,
  input  in_16,
  output O0,
  output O1,
  output O2,
  output O3,
  output O4,
  output O5,
  output O6,
  output O7
);

  xor xor_1 (O0, in_1, in_9);
  xor xor_2 (O1, in_2, in_10);
  xor xor_3 (O2, in_3, in_11);
  xor xor_4 (O3, in_4, in_12);
  xor xor_5 (O4, in_5, in_13);
  xor xor_6 (O5, in_6, in_14);
  xor xor_7 (O6, in_7, in_15);
  xor xor_8 (O7, in_8, in_16);

  // Notes on the sheet:
  //   I0
  //   I1
endmodule

module _4_1_MUX (
  input  in_00,
  input  in_01,
  input  in_10,
  input  in_11,
  input  sel_0,
  input  sel_1,
  output out
);

  wire n2_1_mux_1_out_4, n2_1_mux_2_out_4;

  _2_1_MUX u_2_1_mux_1 (.in_0(in_00), .in_2(in_01), .select(sel_1), .out_4(n2_1_mux_1_out_4));
  _2_1_MUX u_2_1_mux_2 (.in_0(in_10), .in_2(in_11), .select(sel_1), .out_4(n2_1_mux_2_out_4));
  _2_1_MUX u_2_1_mux_3 (.in_0(n2_1_mux_1_out_4), .in_2(n2_1_mux_2_out_4), .select(sel_0), .out_4(out));
endmodule

module _2_1_MUX (
  input  in_0,
  input  in_2,
  input  select,
  output out_4
);

  wire and_1_out, and_2_out, not_1_out;

  not not_1 (not_1_out, select);
  and and_1 (and_1_out, in_0, not_1_out);
  and and_2 (and_2_out, in_2, in_2, select);
  or or_1 (out_4, and_1_out, and_1_out, and_2_out, and_2_out);
endmodule
