// Logisim project 8_1_MUX.circ as structural Verilog: 6 circuits, main circuit main
module main (
  input  in_1,
  input  inputs__A_B_C,
  input  in_3,
  output ABC,
  output A_B_C
);

  AND AND (.in_1(in_1), .in_2(inputs__A_B_C), .in_3(in_3), .out_4(ABC));
  OR OR (.in_1(in_1), .in_2(inputs__A_B_C), .in_3(in_3), .out_4(A_B_C));
endmodule

module _2_1_MUX (
  input  in_0,
  input  in_1,
  input  select,
  output out_4
);

  wire and_1_out, and_2_out, not_1_out;

  not not_1 (not_1_out, select);
  and and_1 (and_1_out, in_0, not_1_out);
  and and_2 (and_2_out, in_1, in_1, select);
  or or_1 (out_4, and_1_out, and_1_out, and_2_out, and_2_out);
endmodule

module _4_1_MUX (
  input  in_00,
  input  in_01,
  input  in_10,
  input  in_11,
  input  sel_0,
  input  sel_1,
  output out
);

  wire n2_1_mux_1_out_4, n2_1_mux_2_out_4;

  _2_1_MUX u_2_1_mux_1 (.in_0(in_00), .in_1(in_01), .select(sel_1), .out_4(n2_1_mux_1_out_4));
  _2_1_MUX u_2_1_mux_2 (.in_0(in_10), .in_1(in_11), .select(sel_1), .out_4(n2_1_mux_2_out_4));
  _2_1_MUX u_2_1_mux_3 (.in_0(n2_1_mux_1_out_4), .in_1(n2_1_mux_2_out_4), .select(sel_0), .out_4(out));
endmodule

module _8_1_MUX (
  input  in_000,
  input  in_001,
  input  in_010,
  input  in_011,
  input  in_100,
  input  in_101,
  input  in_110,
  input  in_111,
  input  sel_2,
  input  sel_1,
  input  sel_0,
  output out_12
);

  wire n2_1_mux_1_out_4, n2_1_mux_2_out_4, n2_1_mux_3_out_4, n2_1_mux_4_out_4, n2_1_mux_5_out_4,
       n2_1_mux_6_out_4;

  _2_1_MUX u_2_1_mux_1 (.in_0(in_000), .in_1(in_001), .select(sel_0), .out_4(n2_1_mux_1_out_4));
  _2_1_MUX u_2_1_mux_2 (.in_0(in_010), .in_1(in_011), .select(sel_0), .out_4(n2_1_mux_2_out_4));
  _2_1_MUX u_2_1_mux_3 (.in_0(in_100), .in_1(in_101), .select(sel_0), .out_4(n2_1_mux_3_out_4));
  _2_1_MUX u_2_1_mux_4 (.in_0(in_110), .in_1(in_111), .select(sel_0), .out_4(n2_1_mux_4_out_4));
  _2_1_MUX u_2_1_mux_5 (.in_0(n2_1_mux_1_out_4), .in_1(n2_1_mux_2_out_4), .select(sel_1), .out_4(n2_1_mux_5_out_4));
  _2_1_MUX u_2_1_mux_6 (.in_0(n2_1_mux_3_out_4), .in_1(n2_1_mux_4_out_4), .select(sel_1), .out_4(n2_1_mux_6_out_4));
  _2_1_MUX u_2_1_mux_7 (.in_0(n2_1_mux_5_out_4), .in_1(n2_1_mux_6_out_4), .select(sel_2), .out_4(out_12));
endmodule

module AND (
  input  in_1,
  input  in_2,
  input  in_3,
  output out_4
);

  wire not_1_out;

  not not_1 (not_1_out, 1'b0);
  _8_1_MUX u_8_1_mux_1 (
    .in_000(1'b0), .in_001(1'b0), .in_010(1'b0), .in_011(1'b0), .in_100(1'b0), .in_101(1'b0), .in_110(1'b0),
    .in_111(not_1_out), .sel_2(in_1), .sel_1(in_2), .sel_0(in_3), .out_12(out_4));
endmodule

module OR (
  input  in_1,
  input  in_2,
  input  in_3,
  output out_4
);

  wire not_1_out, not_2_out;

  not not_1 (not_1_out, 1'b0);
  not not_2 (not_2_out, not_1_out);
  _8_1_MUX u_8_1_mux_1 (
    .in_000(not_2_out), .in_001(not_1_out), .in_010(not_1_out), .in_011(not_1_out), .in_100(not_1_out),
    .in_101(not_1_out), .in_110(not_1_out), .in_111(not_1_out), .sel_2(in_1), .sel_1(in_2), .sel_0(in_3),
    .out_12(out_4));
endmodule
