// Logisim project ALU.circ as structural Verilog: 7 circuits, main circuit main
module main (
  input  cin,
  input  in_2,
  input  in_3,
  input  in_4,
  input  in_5,
  input  \input ,
  input  in_7,
  input  in_8,
  input  in_9,
  input  [2:0] select,
  output \output ,
  output out_12,
  output out_13,
  output cout,
  output out_15
);

  wire ADD_out_10, ADD_out_11, ADD_out_12, ADD_out_13, AND_o0, AND_o1, AND_o2, AND_o3, NOT_o0, NOT_o1,
       NOT_o2, NOT_o3, OR_o0, OR_o1, OR_o2, OR_o3, XOR_o0, XOR_o1, XOR_o2, XOR_o3;

  ADD ADD (
    .in_2(in_5), .in_3(in_4), .in_4(in_3), .in_5(in_2), .in_1(cin), .in_6(in_9), .in_7(in_8), .in_8(in_7),
    .in_9(\input ), .out_14(out_15), .out_10(ADD_out_10), .out_11(ADD_out_11), .out_12(ADD_out_12),
    .out_13(ADD_out_13));
  XOR XOR (
    .in_5(in_9), .in_6(in_8), .in_7(in_7), .in_8(\input ), .in_1(in_5), .in_2(in_4), .in_3(in_3),
    .in_4(in_2), .O0(XOR_o0), .O1(XOR_o1), .O2(XOR_o2), .O3(XOR_o3));
  AND AND (
    .in_5(in_5), .in_6(in_4), .in_7(in_3), .in_8(in_2), .in_1(in_9), .in_2(in_8), .in_3(in_7),
    .in_4(\input ), .O0(AND_o0), .O1(AND_o1), .O2(AND_o2), .O3(AND_o3));
  OR OR (
    .in_5(in_9), .in_6(in_8), .in_7(in_7), .in_8(\input ), .in_1(in_5), .in_2(in_4), .in_3(in_3),
    .in_4(in_2), .O0(OR_o0), .O1(OR_o1), .O2(OR_o2), .O3(OR_o3));
  NOT NOT (.I0(in_5), .in_2(in_4), .in_3(in_3), .in_4(in_2), .O0(NOT_o0), .O1(NOT_o1), .O2(NOT_o2), .O3(NOT_o3));
  Multiplexer #(.select(3), .enable("false")) multiplexer_1 (
    .in0(ADD_out_10), .in1(XOR_o0), .in2(AND_o0), .in3(OR_o0), .in4(NOT_o0), .in5(cin), .in6(cin), .in7(cin),
    .out(cout), .sel(select));
  Multiplexer #(.select(3), .enable("false")) multiplexer_2 (
    .in0(ADD_out_11), .in1(XOR_o1), .in2(AND_o1), .in3(OR_o1), .in4(NOT_o1), .in5(cin), .in6(cin), .in7(cin),
    .out(out_13), .sel(select));
  Multiplexer #(.select(3), .enable("false")) multiplexer_3 (
    .in0(ADD_out_12), .in1(XOR_o2), .in2(AND_o2), .in3(OR_o2), .in4(NOT_o2), .in5(cin), .in6(cin), .in7(cin),
    .out(out_12), .sel(select));
  Multiplexer #(.select(3), .enable("false")) multiplexer_4 (
    .in0(ADD_out_13), .in1(XOR_o3), .in2(AND_o3), .in3(OR_o3), .in4(NOT_o3), .in5(cin), .in6(cin), .in7(cin),
    .out(\output ), .sel(select));
endmodule

module ADD (
  input  in_1,
  input  in_2,
  input  in_3,
  input  in_4,
  input  in_5,
  input  in_6,
  input  in_7,
  input  in_8,
  input  in_9,
  output out_10,
  output out_11,
  output out_12,
  output out_13,
  output out_14
);

  wire adder_1_out_5, adder_2_out_5, adder_3_out_5;

  Adder adder_1 (.in_1(in_1), .in_2(in_6), .in_3(in_2), .out_4(out_10), .out_5(adder_1_out_5));
  Adder adder_2 (.in_1(adder_1_out_5), .in_2(in_7), .in_3(in_3), .out_4(out_11), .out_5(adder_2_out_5));
  Adder adder_3 (.in_1(adder_2_out_5), .in_2(in_4), .in_3(in_8), .out_4(out_12), .out_5(adder_3_out_5));
  Adder adder_4 (.in_1(adder_3_out_5), .in_2(in_5), .in_3(in_9), .out_4(out_13), .out_5(out_14));
endmodule

module XOR (
  input  in_1,
  input  in_2,
  input  in_3,
  input  in_4,
  input  in_5,
  input  in_6,
  input  in_7,
  input  in_8,
  output O0,
  output O1,
  output O2,
  output O3
);

  xor xor_1 (O0, in_1, in_5);
  xor xor_2 (O1, in_2, in_6);
  xor xor_3 (O2, in_3, in_7);
  xor xor_4 (O3, in_4, in_8);

  // Notes on the sheet:
  //   I0
  //   I1
endmodule

module AND (
  input  in_1,
  input  in_2,
  input  in_3,
  input  in_4,
  input  in_5,
  input  in_6,
  input  in_7,
  input  in_8,
  output O0,
  output O1,
  output O2,
  output O3
);

  and and_1 (O0, in_1, in_5);
  and and_2 (O1, in_2, in_6);
  and and_3 (O2, in_3, in_7);
  and and_4 (O3, in_4, in_8);

  // Notes on the sheet:
  //   I0
  //   I1
endmodule

module OR (
  input  in_1,
  input  in_2,
  input  in_3,
  input  in_4,
  input  in_5,
  input  in_6,
  input  in_7,
  input  in_8,
  output O0,
  output O1,
  output O2,
  output O3
);

  or or_1 (O0, in_1, in_5);
  or or_2 (O1, in_2, in_6);
  or or_3 (O2, in_3, in_7);
  or or_4 (O3, in_4, in_8);

  // Notes on the sheet:
  //   I0
  //   I1
endmodule

module NOT (
  input  I0,
  input  in_2,
  input  in_3,
  input  in_4,
  output O0,
  output O1,
  output O2,
  output O3
);

  not not_1 (O0, I0);
  not not_2 (O1, in_2);
  not not_3 (O2, in_3);
  not not_4 (O3, in_4);
endmodule

module Adder (
  input  in_1,
  input  in_2,
  input  in_3,
  output out_4,
  output out_5
);

  wire and_1_out, and_2_out, and_3_out, xor_1_out, xor_2_out;

  xor xor_1 (xor_1_out, in_1, in_2);
  ExactlyOne xor_2 (.out(xor_2_out), .in1(in_1), .in2(in_2), .in3(in_3));
  and and_1 (and_1_out, in_1, in_2, in_3);
  and and_2 (and_2_out, xor_1_out, in_3);
  and and_3 (and_3_out, in_1, in_2);
  or or_1 (out_4, xor_2_out, and_1_out);
  or or_2 (out_5, and_2_out, and_3_out);
endmodule
