// Logisim project BarrelShifter.circ as structural Verilog: 2 circuits, main circuit main
module main (
  input  x0,
  input  x1,
  input  x2,
  input  in_4,
  input  in_5,
  input  in_6,
  output y3,
  output y2,
  output y1,
  output y0
);

  wire decoder_1_out_3, decoder_1_out_4, decoder_1_out_5, decoder_1_out_6;

  Decoder decoder_1 (
    .in_1(in_5), .in_2(in_6), .out_3(decoder_1_out_3), .out_4(decoder_1_out_4), .out_5(decoder_1_out_5),
    .out_6(decoder_1_out_6));
  assign y3 = decoder_1_out_6 ? x0 : 1'bz;  // Controlled_Buffer controlled_buffer_1
  assign y2 = decoder_1_out_5 ? x0 : 1'bz;  // Controlled_Buffer controlled_buffer_2
  assign y1 = decoder_1_out_4 ? x0 : 1'bz;  // Controlled_Buffer controlled_buffer_3
  assign y0 = decoder_1_out_3 ? x0 : 1'bz;  // Controlled_Buffer controlled_buffer_4
  assign y3 = decoder_1_out_5 ? x1 : 1'bz;  // Controlled_Buffer controlled_buffer_5
  assign y2 = decoder_1_out_4 ? x1 : 1'bz;  // Controlled_Buffer controlled_buffer_6
  assign y1 = decoder_1_out_3 ? x1 : 1'bz;  // Controlled_Buffer controlled_buffer_7
  assign y0 = decoder_1_out_6 ? x1 : 1'bz;  // Controlled_Buffer controlled_buffer_8
  assign y3 = decoder_1_out_4 ? x2 : 1'bz;  // Controlled_Buffer controlled_buffer_9
  assign y2 = decoder_1_out_3 ? x2 : 1'bz;  // Controlled_Buffer controlled_buffer_10
  assign y1 = decoder_1_out_6 ? x2 : 1'bz;  // Controlled_Buffer controlled_buffer_11
  assign y0 = decoder_1_out_5 ? x2 : 1'bz;  // Controlled_Buffer controlled_buffer_12
  assign y3 = decoder_1_out_3 ? in_4 : 1'bz;  // Controlled_Buffer controlled_buffer_13
  assign y2 = decoder_1_out_6 ? in_4 : 1'bz;  // Controlled_Buffer controlled_buffer_14
  assign y1 = decoder_1_out_5 ? in_4 : 1'bz;  // Controlled_Buffer controlled_buffer_15
  assign y0 = decoder_1_out_4 ? in_4 : 1'bz;  // Controlled_Buffer controlled_buffer_16

  // Notes on the sheet:
  //   Shifts
  //   x3
endmodule

module Decoder (
  input  in_1,
  input  in_2,
  output out_3,
  output out_4,
  output out_5,
  output out_6
);

  wire not_1_out, not_2_out;

  not not_1 (not_1_out, in_1);
  not not_2 (not_2_out, in_2);
  and and_1 (out_3, not_1_out, not_2_out);
  and and_2 (out_4, not_1_out, in_2);
  and and_3 (out_5, in_1, not_2_out);
  and and_4 (out_6, in_2, in_1);
endmodule
