// Logisim project CLA.circ as structural Verilog: 4 circuits, main circuit main
module main (
  input  inp_1,
  input  in_2,
  input  in_3,
  input  in_4,
  input  in_5,
  input  in_6,
  input  in_7,
  input  in_8,
  input  inp_2,
  input  in_10,
  input  in_11,
  input  in_12,
  input  in_13,
  input  in_14,
  input  in_15,
  input  in_16,
  input  cin,
  output \output ,
  output out_19,
  output out_20,
  output out_21,
  output out_22,
  output out_23,
  output out_24,
  output out_25
);

  _8bit_CLA u_8bit_cla_1 (
    .out_18(\output ), .out_19(out_19), .out_20(out_20), .out_21(out_21), .out_22(out_22), .out_23(out_23),
    .out_24(out_24), .out_25(out_25), .in_10(inp_1), .in_11(in_2), .in_12(in_3), .in_13(in_4), .in_14(in_5),
    .in_15(in_6), .in_16(in_7), .in_17(in_8), .in_1(inp_2), .in_2(in_10), .in_3(in_11), .in_4(in_12),
    .in_5(in_13), .in_6(in_14), .in_7(in_15), .in_8(in_16), .in_9(cin));
endmodule

module _4bit_CLA (
  input  in_1,
  input  in_2,
  input  in_3,
  input  in_4,
  input  in_5,
  input  in_6,
  input  in_7,
  input  in_8,
  input  in_9,
  output out_10,
  output out_11,
  output out_12,
  output out_13,
  output out_14
);

  wire and_1_out, and_2_out, and_3_out, and_4_out, and_5_out, and_6_out, and_7_out, and_8_out, and_9_out,
       or_1_out, or_2_out, or_3_out, xor_1_out, xor_2_out, xor_3_out;

  and and_1 (and_1_out, in_8, in_4);
  and and_2 (and_2_out, in_7, in_3);
  and and_3 (and_3_out, in_9, in_5);
  xor xor_1 (xor_1_out, in_9, in_5);
  xor xor_2 (xor_2_out, in_8, in_4);
  xor xor_3 (xor_3_out, in_7, in_3);
  or or_1 (or_1_out, and_3_out, and_4_out);
  and and_4 (and_4_out, in_1, xor_1_out);
  and and_5 (and_5_out, xor_1_out, in_1, xor_2_out);
  and and_6 (and_6_out, and_3_out, xor_2_out);
  and and_7 (and_7_out, in_1, xor_2_out, xor_3_out, xor_1_out);
  and and_8 (and_8_out, xor_2_out, xor_3_out, and_3_out);
  and and_9 (and_9_out, xor_3_out, and_1_out);
  or or_2 (or_2_out, and_5_out, and_6_out, and_1_out);
  or or_3 (or_3_out, and_7_out, and_2_out, and_8_out, and_9_out);
  FullAdder fulladder_1 (.in_1(in_1), .in_2(in_5), .in_3(in_9), .out_4(out_10));  // open: out_5
  FullAdder fulladder_2 (.in_1(or_1_out), .in_2(in_4), .in_3(in_8), .out_4(out_11));  // open: out_5
  FullAdder fulladder_3 (.in_1(or_2_out), .in_2(in_3), .in_3(in_7), .out_4(out_12));  // open: out_5
  FullAdder fulladder_4 (.in_1(or_3_out), .in_2(in_2), .in_3(in_6), .out_4(out_13), .out_5(out_14));
endmodule

module FullAdder (
  input  in_1,
  input  in_2,
  input  in_3,
  output out_4,
  output out_5
);

  wire and_1_out, and_2_out, xor_1_out;

  xor xor_1 (xor_1_out, in_1, in_2);
  xor xor_2 (out_4, xor_1_out, in_3);
  and and_1 (and_1_out, xor_1_out, in_3);
  and and_2 (and_2_out, in_2, in_1);
  or or_1 (out_5, and_1_out, and_2_out);
endmodule

module _8bit_CLA (
  input  in_1,
  input  in_2,
  input  in_3,
  input  in_4,
  input  in_5,
  input  in_6,
  input  in_7,
  input  in_8,
  input  in_9,
  input  in_10,
  input  in_11,
  input  in_12,
  input  in_13,
  input  in_14,
  input  in_15,
  input  in_16,
  input  in_17,
  output out_18,
  output out_19,
  output out_20,
  output out_21,
  output out_22,
  output out_23,
  output out_24,
  output out_25
);

  wire n4bit_cla_2_out_14;

  _4bit_CLA u_4bit_cla_1 (
    .in_6(in_10), .in_7(in_11), .in_8(in_12), .in_9(in_13), .in_1(n4bit_cla_2_out_14), .in_2(in_1),
    .in_3(in_2), .in_4(in_3), .in_5(in_4), .out_10(out_21), .out_11(out_20), .out_12(out_19), .out_13(out_18));  // open: out_14
  _4bit_CLA u_4bit_cla_2 (
    .in_6(in_14), .in_7(in_15), .in_8(in_16), .in_9(in_17), .in_1(in_9), .in_2(in_5), .in_3(in_6),
    .in_4(in_7), .in_5(in_8), .out_14(n4bit_cla_2_out_14), .out_10(out_25), .out_11(out_24), .out_12(out_23),
    .out_13(out_22));
endmodule
