// Logisim project Subcircuits.circ as structural Verilog: 4 circuits, main circuit main
module main (
  input  inputs,
  input  in_01,
  input  in_10,
  input  in_11,
  input  sel_0,
  input  sel_1,
  output \output 
);

  _4_1_MUX _4_1_MUX (
    .in_00(inputs), .in_01(in_01), .in_10(in_10), .in_11(in_11), .sel_0(sel_0), .sel_1(sel_1), .out(\output ));

  // Notes on the sheet:
  //   in 00
  //   select
endmodule

module _2_1_MUX (
  input  in_0,
  input  in_1,
  input  select,
  output out_4
);

  wire and_1_out, and_2_out, not_1_out;

  not not_1 (not_1_out, select);
  and and_1 (and_1_out, in_0, not_1_out);
  and and_2 (and_2_out, in_1, in_1, select);
  or or_1 (out_4, and_1_out, and_1_out, and_2_out, and_2_out);
endmodule

module _4_1_MUX (
  input  in_00,
  input  in_01,
  input  in_10,
  input  in_11,
  input  sel_0,
  input  sel_1,
  output out
);

  wire n2_1_mux_1_out_4, n2_1_mux_2_out_4;

  _2_1_MUX u_2_1_mux_1 (.in_0(in_00), .in_1(in_01), .select(sel_1), .out_4(n2_1_mux_1_out_4));
  _2_1_MUX u_2_1_mux_2 (.in_0(in_10), .in_1(in_11), .select(sel_1), .out_4(n2_1_mux_2_out_4));
  _2_1_MUX u_2_1_mux_3 (.in_0(n2_1_mux_1_out_4), .in_1(n2_1_mux_2_out_4), .select(sel_0), .out_4(out));
endmodule

module _4_1_MUX2 (
  input  in_00,
  input  in_01,
  input  in_10,
  input  in_11,
  input  select,
  input  in_6,
  output out_7
);

  wire and_1_out, and_2_out, and_3_out, and_4_out, not_1_out, not_2_out, not_3_out, not_4_out, or_1_out,
       or_2_out;

  not not_1 (not_1_out, in_6);
  not not_2 (not_2_out, select);
  not not_3 (not_3_out, select);
  not not_4 (not_4_out, in_6);
  and and_1 (and_1_out, in_00, not_1_out, not_2_out);
  and and_2 (and_2_out, in_01, in_01, not_3_out, in_6);
  and and_3 (and_3_out, in_10, select, not_4_out);
  and and_4 (and_4_out, in_11, in_11, select, in_6);
  or or_1 (or_1_out, and_1_out, and_1_out, and_2_out, and_2_out);
  or or_2 (or_2_out, and_3_out, and_3_out, and_4_out, and_4_out);
  or or_3 (out_7, or_1_out, or_2_out);
endmodule
