// Logisim project Adder_Carry.circ as structural Verilog: 2 circuits, main circuit main
module main (
  input  carry_in,
  input  in_2,
  input  in_3,
  input  in_4,
  input  in_5,
  input  in_6,
  input  in_7,
  input  in_8,
  input  in_9,
  output outputs,
  output out_11,
  output out_12,
  output out_13
);

  wire adder_1_carry, adder_2_carry, adder_3_carry;

  Adder adder_1 (.A(carry_in), .B(in_6), .carry_in(in_2), .Sum(outputs), .Carry(adder_1_carry));
  Adder adder_2 (.A(adder_1_carry), .B(in_7), .carry_in(in_3), .Sum(out_11), .Carry(adder_2_carry));
  Adder adder_3 (.A(adder_2_carry), .B(in_4), .carry_in(in_8), .Sum(out_12), .Carry(adder_3_carry));
  Adder adder_4 (.A(adder_3_carry), .B(in_5), .carry_in(in_9), .Sum(out_13));  // open: Carry

  // Notes on the sheet:
  //   inputs
endmodule

module Adder (
  input  A,
  input  B,
  input  carry_in,
  output Sum,
  output Carry
);

  wire and_1_out, and_2_out, xor_1_out, xor_2_out;

  xor xor_1 (xor_1_out, A, B);
  xor xor_2 (xor_2_out, A, B);
  and and_1 (and_1_out, xor_1_out, carry_in);
  and and_2 (and_2_out, A, B);
  xor xor_3 (Sum, xor_2_out, carry_in);
  or or_1 (Carry, and_1_out, and_2_out);
endmodule
