// Logisim project RegFile.circ as structural Verilog
module _4_4bit___1w_1r (
  input  Read_Write,
  input  [1:0] Address,
  input  [3:0] Data,
  input  Clock,
  output [3:0] Read_Value
);

  wire and_1_out, and_2_out, and_3_out, and_4_out, decoder_1_out0, decoder_1_out1, decoder_1_out2,
       decoder_1_out3, not_1_out;
  wire [3:0] register_1_q, register_2_q, register_3_q, register_4_q;

  Decoder #(.select(2)) decoder_1 (
    .out0(decoder_1_out0), .out1(decoder_1_out1), .out2(decoder_1_out2), .out3(decoder_1_out3), .sel(Address));  // open: en
  and and_1 (and_1_out, decoder_1_out0, Read_Write);
  and and_2 (and_2_out, decoder_1_out1, Read_Write);
  and and_3 (and_3_out, decoder_1_out2, Read_Write);
  and and_4 (and_4_out, decoder_1_out3, Read_Write);
  not not_1 (not_1_out, Read_Write);
  Register #(.width(4), .trigger("high")) register_1 (
    .D(Data), .en(and_1_out), .Q(register_1_q), .clk(Clock));  // open: clr
  Register #(.width(4), .trigger("high")) register_2 (
    .D(Data), .en(and_2_out), .Q(register_2_q), .clk(Clock));  // open: clr
  Register #(.width(4), .trigger("high")) register_3 (
    .D(Data), .en(and_3_out), .Q(register_3_q), .clk(Clock));  // open: clr
  Register #(.width(4), .trigger("high")) register_4 (
    .D(Data), .en(and_4_out), .Q(register_4_q), .clk(Clock));  // open: clr
  Multiplexer #(.select(2), .width(4)) multiplexer_1 (
    .in0(register_1_q), .in1(register_2_q), .in2(register_3_q), .in3(register_4_q), .out(Read_Value),
    .sel(Address), .en(not_1_out));

  // Notes on the sheet:
  //   Registors
endmodule

module _8_16bit___1w_2r (
  input  Read_Write,
  input  [2:0] in_2,
  input  [15:0] in_3,
  input  [2:0] in_4,
  input  [2:0] Read2,
  input  Clock,
  output [15:0] out_7,
  output [15:0] out_8
);

  wire and_1_out, and_2_out, and_3_out, and_4_out, and_5_out, and_6_out, and_7_out, and_8_out,
       decoder_1_out0, decoder_1_out1, decoder_1_out2, decoder_1_out3, decoder_1_out4, decoder_1_out5,
       decoder_1_out6, decoder_1_out7, not_1_out;
  wire [15:0] register_1_q, register_2_q, register_3_q, register_4_q, register_5_q, register_6_q,
       register_7_q, register_8_q;

  Decoder #(.select(3)) decoder_1 (
    .out0(decoder_1_out0), .out1(decoder_1_out1), .out2(decoder_1_out2), .out3(decoder_1_out3),
    .out4(decoder_1_out4), .out5(decoder_1_out5), .out6(decoder_1_out6), .out7(decoder_1_out7), .sel(in_2));  // open: en
  not not_1 (not_1_out, Read_Write);
  and and_1 (and_1_out, decoder_1_out0, Read_Write);
  and and_2 (and_2_out, decoder_1_out1, Read_Write);
  and and_3 (and_3_out, decoder_1_out2, Read_Write);
  and and_4 (and_4_out, decoder_1_out3, Read_Write);
  and and_5 (and_5_out, decoder_1_out4, Read_Write);
  and and_6 (and_6_out, decoder_1_out5, Read_Write);
  and and_7 (and_7_out, decoder_1_out6, Read_Write);
  and and_8 (and_8_out, decoder_1_out7, Read_Write);
  Register #(.width(16), .trigger("high")) register_1 (
    .D(in_3), .en(and_1_out), .Q(register_1_q), .clk(Clock));  // open: clr
  Register #(.width(16), .trigger("high")) register_2 (
    .D(in_3), .en(and_2_out), .Q(register_2_q), .clk(Clock));  // open: clr
  Register #(.width(16), .trigger("high")) register_3 (
    .D(in_3), .en(and_3_out), .Q(register_3_q), .clk(Clock));  // open: clr
  Register #(.width(16), .trigger("high")) register_4 (
    .D(in_3), .en(and_4_out), .Q(register_4_q), .clk(Clock));  // open: clr
  Register #(.width(16), .trigger("high")) register_5 (
    .D(in_3), .en(and_5_out), .Q(register_5_q), .clk(Clock));  // open: clr
  Register #(.width(16), .trigger("high")) register_6 (
    .D(in_3), .en(and_6_out), .Q(register_6_q), .clk(Clock));  // open: clr
  Register #(.width(16), .trigger("high")) register_7 (
    .D(in_3), .en(and_7_out), .Q(register_7_q), .clk(Clock));  // open: clr
  Register #(.width(16), .trigger("high")) register_8 (
    .D(in_3), .en(and_8_out), .Q(register_8_q), .clk(Clock));  // open: clr
  Multiplexer #(.select(3), .width(16)) multiplexer_1 (
    .in0(register_1_q), .in1(register_2_q), .in2(register_3_q), .in3(register_4_q), .in4(register_5_q),
    .in5(register_6_q), .in6(register_7_q), .in7(register_8_q), .out(out_7), .sel(in_4), .en(not_1_out));
  Multiplexer #(.select(3), .width(16)) multiplexer_2 (
    .in0(register_1_q), .in1(register_2_q), .in2(register_3_q), .in3(register_4_q), .in4(register_5_q),
    .in5(register_6_q), .in6(register_7_q), .in7(register_8_q), .out(out_8), .sel(Read2), .en(not_1_out));

  // Notes on the sheet:
  //   Write
  //   Data
  //   Read1
  //   Registors
  //   Read 1
  //   Read 2
endmodule
